# Fritzing sketch DustEstimator (saved by Fritzing 0.9.3b)
breadboards: 1

parts:
  부품1 = Arduino Nano (Rev3.0)
  R1 = Resistor [tolerance=±5% resistance=150 package=THT]
  U1 = Sharp Dust Sensor [part_number=GP2Y1010AU0F]
  C1 = Electrolytic Capacitor [capacitance=220µF voltage=6.3V package="100 mil [THT, electrolytic]"]
  J2 = male pin header, 3 pins [form="♂ (male)"]
  LED1 = LED - 5mm [color="Orange (612nm)" package="5 mm [THT]"]
  LED2 = LED - 5mm [color="Red (633nm)" package="5 mm [THT]"]
  LED3 = LED - 5mm [color="Green (570nm)" package="5 mm [THT]"]
  LED4 = LED - 5mm [color="Blue (505nm)" package="5 mm [THT]"]
  R2 = Resistor [tolerance=±5% resistance=220 package=THT]
  LCD1 = LCD screen
  LCM1602_IIC2 = LCM1602 IIC [part_number="LCM1602 IIC" chip_label="LCM1602 IIC" package="DIP (Dual Inline) [THT]"]

nets:
  GND: 부품1.GND, U1.LED-GND, U1.S-GND, C1.-, J2.pin1, R2.Pin_1, LCM1602_IIC2.GND
  N1: 부품1.D5, LED2.anode
  N2: 부품1.D6, LED1.anode
  N3: 부품1.D7, LED3.anode
  N4: 부품1.D8, LED4.anode
  N5: 부품1.D11/MOSI, J2.pin2
  N6: 부품1.D12/MISO, U1.LED
  VCC: 부품1.5V, R1.Pin_0, U1.VCC, J2.pin3, LCM1602_IIC2.VCC
  N7: 부품1.A5, LCM1602_IIC2.SCL
  N8: 부품1.A4, LCM1602_IIC2.SDA
  N9: 부품1.A0, U1.Vo
  N10: R1.Pin_1, U1.V-LED, C1.+
  N11: LED1.cathode, LED2.cathode, LED4.cathode, R2.Pin_0
  VSS: LCD1.VSS, LCM1602_IIC2.VSS
  VDD: LCD1.VDD, LCM1602_IIC2.VDD
  N12: LCD1.V0, LCM1602_IIC2.V0
  N13: LCD1.RS, LCM1602_IIC2.RS
  N14: LCD1.R/W, LCM1602_IIC2.RW
  N15: LCD1.E, LCM1602_IIC2.E
  N16: LCD1.DB0, LCM1602_IIC2.D0
  N17: LCD1.DB1, LCM1602_IIC2.D1
  N18: LCD1.DB2, LCM1602_IIC2.D2
  N19: LCD1.DB3, LCM1602_IIC2.D3
  N20: LCD1.DB4, LCM1602_IIC2.D4
  N21: LCD1.DB5, LCM1602_IIC2.D5
  N22: LCD1.DB6, LCM1602_IIC2.D6
  N23: LCD1.DB7, LCM1602_IIC2.D7
  N24: LCD1.LED+, LCM1602_IIC2.A
  N25: LCD1.LED-, LCM1602_IIC2.K
  N26: LCM1602_IIC2.LED_A, LCM1602_IIC2.LED_B

custom parts:
  Sharp Dust Sensor: Sharp GP2Y1010AU0F Dust Sensor
  LCM1602 IIC: I2C-Module to use a 1602 or 2004 LCD on with the wire.h libory Serial LCD Modul
